# Fritzing sketch Untitled Sketch (saved by Fritzing 0.8.5b)
perfboards: 1

parts:
  M1 = DC Motor
  Q1 = PHOTOTRANSISTOR REFLECTIVE OBJECT SENSOR [package=qrb1114-side]
  Q2 = PHOTOTRANSISTOR REFLECTIVE OBJECT SENSOR [package=qrb1114-side]
  J1 = Power Jack [package=power_jack_combo]
  U4 = RELAY-2 [package=relay-g5v]
  U5 = Voltage Regulator - 5V [package="DPak [SMD]"]
  Q3 = NPN-Transistor [package="TO92 [THT]"]
  C2 = Ceramic Capacitor [capacitance=0.1µF package="1206 [SMD, multilayer]"]
  C3 = Ceramic Capacitor [capacitance=22µF package="1206 [SMD, multilayer]"]
  LED1 = LEDs [package=led10mm]
  LED2 = LEDs [package=led10mm]  # not connected
  LED3 = LEDs [package=led10mm]
  LED4 = LEDs [package=led10mm]  # not connected
  R1 = Resistor [tolerance=±5% resistance=220 package=THT]
  Raspberry_Pi_B_rev1 = Raspberry Pi B rev1
  R2 = Resistor [tolerance=±5% resistance=220 package=THT]
  D3 = Rectifier Diode [package="Melf DO-213 AA [SMD]"]
  R3 = Resistor [tolerance=±5% resistance=220 package=THT]
  R4 = Resistor [tolerance=±5% resistance=220 package=THT]
  R5 = Resistor [tolerance=±5% resistance=10k package=THT]
  R6 = Resistor [tolerance=±5% resistance=10k package=THT]
  R7 = Resistor [tolerance=±5% resistance=10k package=THT]
  R8 = Resistor [tolerance=±5% resistance=10k package=THT]

nets:
  N1: M1.pin_2, U4.6
  N2: Q1.A, R3.Pin_1
  N3: Q1.C, Q2.C, Raspberry_Pi_B_rev1.3V3
  N4: Q1.E, R6.Pin_1, R7.Pin_0
  N5: Q1.K, Q2.K, Q3.E, Raspberry_Pi_B_rev1.GND, R5.Pin_0, R6.Pin_0
  N6: Q2.A, R4.Pin_1
  N7: Q2.E, R5.Pin_1, R8.Pin_0
  N8: J1.GND, U4.1, U5.input_voltage, C3.0
  N9: J1.PWR, U4.10, U5.GND, C2.1, C3.1, LED3.C
  N10: U4.2, Q3.C, D3.anode
  N11: U4.9, Raspberry_Pi_B_rev1.5V, D3.cathode, R3.Pin_0, R4.Pin_0
  N12: U5.output_voltage, C2.0, R1.Pin_0
  N13: Q3.B, R2.Pin_1
  N14: LED1.A, R1.Pin_1
  N15: Raspberry_Pi_B_rev1.GPIO_23, R8.Pin_1
  N16: Raspberry_Pi_B_rev1.GPIO_24, R7.Pin_1
  N17: Raspberry_Pi_B_rev1.GPIO_25, R2.Pin_0

notes:
  DC Motor mit integrierte Getriebe
  Antrieb Filmprojektor
  12 V DC In
  Hintergrund Beleuchtung des Film
  Lichtschranke
  Überwachung
  Lichtschranke Drehscheibe
